# Fritzing sketch OximeterBackup (saved by Fritzing 0.8.7b)
breadboards: 2

parts:
  Arduino = Arduino Nano (Rev3.0)
  LCD1 = LCD screen
  Red_LED = LED - 5mm [color="Red (633nm)" package="5 mm [THT]"]
  IR_LED = LTE-302 [package=lte-302]
  Q1 = LTR-301 [package=ltr-301]
  R1 = Resistor [tolerance=±5% resistance=330 package=THT]
  R2 = Resistor [tolerance=±5% resistance=22k package=THT]
  Red_LED_2 = LED - 5mm [color="Red (633nm)" package="5 mm [THT]"]
  Biela_LED = LEDs [package=led10mm]
  R3 = Resistor [tolerance=±5% resistance=330 package=THT]
  R4 = Resistor [tolerance=±5% resistance=330 package=THT]
  R5 = Resistor [tolerance=±5% resistance=330 package=THT]
  MQ1 = GAS_SENSOR [package=mq-7]
  Q2 = TRANSISTOR_NPN [package=to-92-ammo]
  R6 = Resistor [tolerance=±5% resistance=1k package=THT]

nets:
  GND: Arduino.GND, LCD1.VSS, LCD1.V0, LCD1.R/W, Red_LED.cathode, IR_LED.C, Q1.E, Red_LED_2.cathode, Biela_LED.C, MQ1.GND
  N1: Arduino.D2, LCD1.DB7
  N2: Arduino.D3, LCD1.LED-
  N3: Arduino.D4, LCD1.DB5
  N4: Arduino.D5, LCD1.DB4
  N5: Arduino.D7, LCD1.E
  N6: Arduino.D8, LCD1.DB6
  N7: Arduino.D9, R6.Pin_0
  N8: Arduino.D10, R5.Pin_0
  N9: Arduino.D12/MISO, LCD1.RS
  5V: Arduino.5V, LCD1.VDD, R2.Pin_1, R3.Pin_0, Q2.C
  N10: Arduino.A1, MQ1.A0
  N11: Arduino.A0, Q1.C, R2.Pin_0
  N12: Arduino.3V3, LCD1.LED+
  N13: Arduino.D13/SCK, R1.Pin_1, R4.Pin_0
  N14: Red_LED.anode, R1.Pin_0
  N15: IR_LED.A, R5.Pin_1
  N16: Red_LED_2.anode, R4.Pin_1
  N17: Biela_LED.A, R3.Pin_1
  N18: MQ1.Vcc, Q2.E
  N19: Q2.B, R6.Pin_1

custom parts:
  GAS_SENSOR: MQ-7 CO gas sensor .
